// Logisim project Aula_1.circ as structural Verilog: 3 circuits, main circuit main
module main (
  input  [3:0] A,
  input  [3:0] B,
  output [3:0] S
);

  wire somador_completo_2_cout, somador_completo_3_cout, somador_completo_4_cout;

  Somador_Completo somador_completo_1 (.S(S[3]), .Cin(somador_completo_2_cout), .B(B[3]), .A(A[3]));  // open: Cout
  Somador_Completo somador_completo_2 (
    .Cout(somador_completo_2_cout), .S(S[2]), .Cin(somador_completo_3_cout), .B(B[2]), .A(A[2]));
  Somador_Completo somador_completo_3 (
    .Cout(somador_completo_3_cout), .S(S[1]), .Cin(somador_completo_4_cout), .B(B[1]), .A(A[1]));
  Somador_Completo somador_completo_4 (.Cout(somador_completo_4_cout), .S(S[0]), .Cin(1'b0), .B(B[0]), .A(A[0]));
  Hex_Digit_Display hex_digit_display_1 (.value(S));  // open: dp
endmodule

module Meio_somador (
  input  A,
  input  B,
  output S,
  output Cout
);

  xor xor_1 (S, A, B);
  and and_1 (Cout, A, B);
endmodule

module Somador_Completo (
  input  A,
  input  B,
  input  Cin,
  output S,
  output Cout
);

  wire meio_somador_1_cout, meio_somador_1_s, meio_somador_2_cout;

  Meio_somador meio_somador_1 (.Cout(meio_somador_1_cout), .S(meio_somador_1_s), .B(B), .A(A));
  Meio_somador meio_somador_2 (.Cout(meio_somador_2_cout), .S(S), .B(Cin), .A(meio_somador_1_s));
  or or_1 (Cout, meio_somador_2_cout, meio_somador_1_cout);
endmodule
