// Logisim project Aula_2.circ as structural Verilog: 4 circuits, main circuit main
module main (
  input  [3:0] A,
  input  [3:0] B,
  output [3:0] S
);

  wire somador_completo_2_cout, somador_completo_3_cout, somador_completo_4_cout;

  Somador_Completo somador_completo_1 (.Cin(somador_completo_2_cout), .A(A[3]), .B(B[3]), .S(S[3]));  // open: Cout
  Somador_Completo somador_completo_2 (
    .Cout(somador_completo_2_cout), .Cin(somador_completo_3_cout), .A(A[2]), .B(B[2]), .S(S[2]));
  Somador_Completo somador_completo_3 (
    .Cout(somador_completo_3_cout), .Cin(somador_completo_4_cout), .A(A[1]), .B(B[1]), .S(S[1]));
  Somador_Completo somador_completo_4 (.Cout(somador_completo_4_cout), .Cin(1'b0), .A(A[0]), .B(B[0]), .S(S[0]));
  Hex_Digit_Display hex_digit_display_1 (.value(S));  // open: dp
endmodule

module Meio_somador (
  input  A,
  input  B,
  output S,
  output Cout
);

  xor xor_1 (S, A, B);
  and and_1 (Cout, A, B);
endmodule

module Somador_Completo (
  input  A,
  input  B,
  input  Cin,
  output S,
  output Cout
);

  wire meio_somador_1_cout, meio_somador_1_s, meio_somador_2_cout;

  Meio_somador meio_somador_1 (.Cout(meio_somador_1_cout), .B(B), .S(meio_somador_1_s), .A(A));
  Meio_somador meio_somador_2 (.Cout(meio_somador_2_cout), .B(Cin), .S(S), .A(meio_somador_1_s));
  or or_1 (Cout, meio_somador_2_cout, meio_somador_1_cout);
endmodule

module Complemento_2 (
  input  [3:0] A,
  input  [3:0] B,
  input  Cin,
  output Cout,
  output [3:0] S
);

  wire multiplexer_1_out, multiplexer_2_out, multiplexer_3_out, multiplexer_4_out, not_1_out, not_2_out,
       not_3_out, not_4_out, somador_completo_2_cout, somador_completo_3_cout, somador_completo_4_cout;

  not not_1 (not_1_out, B[3]);
  Multiplexer #(.enable("false")) multiplexer_1 (.in0(B[3]), .in1(not_1_out), .out(multiplexer_1_out), .sel(Cin));
  Somador_Completo somador_completo_1 (
    .Cout(Cout), .Cin(somador_completo_2_cout), .A(A[3]), .B(multiplexer_1_out), .S(S[3]));
  Hex_Digit_Display hex_digit_display_1 (.value(S));  // open: dp
  not not_2 (not_2_out, B[2]);
  Multiplexer #(.enable("false")) multiplexer_2 (.in0(B[2]), .in1(not_2_out), .out(multiplexer_2_out), .sel(Cin));
  Somador_Completo somador_completo_2 (
    .Cout(somador_completo_2_cout), .Cin(somador_completo_3_cout), .A(A[2]), .B(multiplexer_2_out), .S(S[2]));
  not not_3 (not_3_out, B[1]);
  Multiplexer #(.enable("false")) multiplexer_3 (.in0(B[1]), .in1(not_3_out), .out(multiplexer_3_out), .sel(Cin));
  Somador_Completo somador_completo_3 (
    .Cout(somador_completo_3_cout), .Cin(somador_completo_4_cout), .A(A[1]), .B(multiplexer_3_out), .S(S[1]));
  not not_4 (not_4_out, B[0]);
  Multiplexer #(.enable("false")) multiplexer_4 (.in0(B[0]), .in1(not_4_out), .out(multiplexer_4_out), .sel(Cin));
  Somador_Completo somador_completo_4 (
    .Cout(somador_completo_4_cout), .Cin(Cin), .A(A[0]), .B(multiplexer_4_out), .S(S[0]));
endmodule
