// Logisim project Relatorio1 Pedro Balestra.circ as structural Verilog: 7 circuits, main circuit main
module main (
  input  [3:0] A,
  input  [3:0] B,
  output [3:0] S
);

  wire somador_completo_2_cout, somador_completo_3_cout, somador_completo_4_cout;

  Somador_Completo somador_completo_1 (.Cin(somador_completo_2_cout), .A(A[3]), .B(B[3]), .S(S[3]));  // open: Cout
  Somador_Completo somador_completo_2 (
    .Cout(somador_completo_2_cout), .Cin(somador_completo_3_cout), .A(A[2]), .B(B[2]), .S(S[2]));
  Somador_Completo somador_completo_3 (
    .Cout(somador_completo_3_cout), .Cin(somador_completo_4_cout), .A(A[1]), .B(B[1]), .S(S[1]));
  Somador_Completo somador_completo_4 (.Cout(somador_completo_4_cout), .Cin(1'b0), .A(A[0]), .B(B[0]), .S(S[0]));
  Hex_Digit_Display hex_digit_display_1 (.value(S));  // open: dp
endmodule

module Meio_somador (
  input  A,
  input  B,
  output S,
  output Cout
);

  xor xor_1 (S, A, B);
  and and_1 (Cout, A, B);
endmodule

module Somador_Completo (
  input  A,
  input  B,
  input  Cin,
  output S,
  output Cout
);

  wire meio_somador_1_cout, meio_somador_1_s, meio_somador_2_cout;

  Meio_somador meio_somador_1 (.Cout(meio_somador_1_cout), .B(B), .S(meio_somador_1_s), .A(A));
  Meio_somador meio_somador_2 (.Cout(meio_somador_2_cout), .B(Cin), .S(S), .A(meio_somador_1_s));
  or or_1 (Cout, meio_somador_2_cout, meio_somador_1_cout);
endmodule

module Meio_Subtrator (
  input  A,
  input  B,
  output S,
  output Tout
);

  wire not_1_out;

  not not_1 (not_1_out, A);
  xor xor_1 (S, A, B);
  and and_1 (Tout, B, not_1_out);
endmodule

module Subtrator_Completo (
  input  A,
  input  B,
  input  Tin,
  output S,
  output Tout
);

  wire meio_subtrator_1_s, meio_subtrator_1_tout, meio_subtrator_2_tout;

  Meio_Subtrator meio_subtrator_1 (.Tout(meio_subtrator_1_tout), .S(meio_subtrator_1_s), .B(B), .A(A));
  Meio_Subtrator meio_subtrator_2 (.Tout(meio_subtrator_2_tout), .S(S), .B(Tin), .A(meio_subtrator_1_s));
  or or_1 (Tout, meio_subtrator_2_tout, meio_subtrator_1_tout);
endmodule

module Exercicio_1 (
  input  A,
  input  B,
  input  K,
  input  C,
  input  D,
  input  K1,
  output S,
  output Cout_Tout,
  output S1,
  output Cout,
  output S2,
  output Tout
);

  wire [1:0] demultiplexer_1_out0, demultiplexer_1_out1, meio_somador_1_s, meio_subtrator_1_s;

  Demultiplexer #(.width(2), .enable("false")) demultiplexer_1 (
    .out0(demultiplexer_1_out0), .out1(demultiplexer_1_out1), .in({D, C}), .sel(K1));
  Meio_somador meio_somador_1 (.Cout(meio_somador_1_s[1]), .B(B), .S(meio_somador_1_s[0]), .A(A));
  Meio_Subtrator meio_subtrator_1 (.Tout(meio_subtrator_1_s[1]), .S(meio_subtrator_1_s[0]), .B(B), .A(A));
  Meio_somador meio_somador_2 (.Cout(Cout), .B(demultiplexer_1_out0[1]), .S(S1), .A(demultiplexer_1_out0[0]));
  Meio_Subtrator meio_subtrator_2 (.Tout(Tout), .S(S2), .B(demultiplexer_1_out1[1]), .A(demultiplexer_1_out1[0]));
  Multiplexer #(.width(2), .enable("false")) multiplexer_1 (
    .in0(meio_somador_1_s), .in1(meio_subtrator_1_s), .out({Cout_Tout, S}), .sel(K));
endmodule

module Exercicio_2 (
  input  A,
  input  B,
  input  K1,
  input  K,
  input  Cin_Tin,
  output S,
  output Cout_Tout
);

  wire [1:0] somador_completo_1_s, subtrator_completo_1_s;
  wire [2:0] demultiplexer_1_out0, demultiplexer_1_out1;

  Demultiplexer #(.width(3), .enable("false")) demultiplexer_1 (
    .out0(demultiplexer_1_out0), .out1(demultiplexer_1_out1), .in({Cin_Tin, B, A}), .sel(K));
  Somador_Completo somador_completo_1 (
    .Cout(somador_completo_1_s[1]), .Cin(demultiplexer_1_out0[2]), .A(demultiplexer_1_out0[0]),
    .B(demultiplexer_1_out0[1]), .S(somador_completo_1_s[0]));
  Subtrator_Completo subtrator_completo_1 (
    .Tout(subtrator_completo_1_s[1]), .S(subtrator_completo_1_s[0]), .Tin(demultiplexer_1_out1[2]),
    .B(demultiplexer_1_out1[1]), .A(demultiplexer_1_out1[0]));
  Multiplexer #(.width(2), .enable("false")) multiplexer_1 (
    .in0(somador_completo_1_s), .in1(subtrator_completo_1_s), .out({Cout_Tout, S}), .sel(K1));
endmodule
