// Logisim project Relatorio2 Pedro Balestra.circ as structural Verilog: 5 circuits, main circuit main
module main (
  input  [3:0] A,
  input  [3:0] B,
  output [3:0] S
);

  wire somador_completo_2_cout, somador_completo_3_cout, somador_completo_4_cout;

  Somador_Completo somador_completo_1 (.A(A[3]), .S(S[3]), .B(B[3]), .Cin(somador_completo_2_cout));  // open: Cout
  Somador_Completo somador_completo_2 (
    .Cout(somador_completo_2_cout), .A(A[2]), .S(S[2]), .B(B[2]), .Cin(somador_completo_3_cout));
  Somador_Completo somador_completo_3 (
    .Cout(somador_completo_3_cout), .A(A[1]), .S(S[1]), .B(B[1]), .Cin(somador_completo_4_cout));
  Somador_Completo somador_completo_4 (.Cout(somador_completo_4_cout), .A(A[0]), .S(S[0]), .B(B[0]), .Cin(1'b0));
  Hex_Digit_Display hex_digit_display_1 (.value(S));  // open: dp
endmodule

module Meio_somador (
  input  A,
  input  B,
  output S,
  output Cout
);

  xor xor_1 (S, A, B);
  and and_1 (Cout, A, B);
endmodule

module Somador_Completo (
  input  A,
  input  B,
  input  Cin,
  output S,
  output Cout
);

  wire meio_somador_1_cout, meio_somador_1_s, meio_somador_2_cout;

  Meio_somador meio_somador_1 (.Cout(meio_somador_1_cout), .S(meio_somador_1_s), .B(B), .A(A));
  Meio_somador meio_somador_2 (.Cout(meio_somador_2_cout), .S(S), .B(Cin), .A(meio_somador_1_s));
  or or_1 (Cout, meio_somador_2_cout, meio_somador_1_cout);
endmodule

module Multiplicador (
  input  A1,
  input  A0,
  input  B1,
  input  B0,
  output P3,
  output P2,
  output P1,
  output P0
);

  wire and_1_out, and_2_out, and_3_out, meio_somador_2_cout;

  and and_1 (and_1_out, A1, B1);
  and and_2 (and_2_out, A1, B0);
  Meio_somador meio_somador_1 (.Cout(P3), .S(P2), .B(and_1_out), .A(meio_somador_2_cout));
  and and_3 (and_3_out, A0, B1);
  and and_4 (P0, A0, B0);
  Meio_somador meio_somador_2 (.Cout(meio_somador_2_cout), .S(P1), .B(and_2_out), .A(and_3_out));
endmodule

module Registrador (
  input  [3:0] D,
  input  Clock,
  input  Carga,
  input  Clear,
  output [3:0] Q
);

  wire multiplexer_1_out, multiplexer_2_out, multiplexer_3_out, multiplexer_4_out;

  D_Flip_Flop d_ff_1 (.D(multiplexer_1_out), .clk(Clock), .Q(Q[0]), .reset(Clear));  // open: Qn, preset
  Multiplexer #(.enable("false")) multiplexer_1 (.in0(Q[0]), .in1(D[0]), .out(multiplexer_1_out), .sel(Carga));
  Multiplexer #(.enable("false")) multiplexer_2 (.in0(Q[1]), .in1(D[1]), .out(multiplexer_2_out), .sel(Carga));
  D_Flip_Flop d_ff_2 (.D(multiplexer_2_out), .clk(Clock), .Q(Q[1]), .reset(Clear));  // open: Qn, preset
  Multiplexer #(.enable("false")) multiplexer_3 (.in0(Q[2]), .in1(D[2]), .out(multiplexer_3_out), .sel(Carga));
  D_Flip_Flop d_ff_3 (.D(multiplexer_3_out), .clk(Clock), .Q(Q[2]), .reset(Clear));  // open: Qn, preset
  Multiplexer #(.enable("false")) multiplexer_4 (.in0(Q[3]), .in1(D[3]), .out(multiplexer_4_out), .sel(Carga));
  D_Flip_Flop d_ff_4 (.D(multiplexer_4_out), .clk(Clock), .Q(Q[3]), .reset(Clear));  // open: Qn, preset
endmodule
