// Logisim project Caminho1.circ as structural Verilog: 1 circuit, main circuit main
module main (
  input  in_1,
  input  [31:0] in_2,
  input  habilita_escrita,
  input  [4:0] End_leitura_REGB,
  input  [4:0] End_escrita,
  input  [4:0] End_leitura_REGA,
  output [5:0] funct,
  output [4:0] sa,
  output [4:0] Reg_destino,
  output [4:0] Origem1,
  output [4:0] Origem2,
  output [5:0] OPCODE,
  output [31:0] Dado_Lido_REGA,
  output [31:0] Dado_Lido_REGB
);

  wire clock_1_out, clock_2_out, registerfile_1_p1;
  wire [31:0] adder_1_out, register_1_q;

  Register #(.width(32)) register_1 (.D(adder_1_out), .clk(clock_1_out), .Q(register_1_q), .clr(in_1));  // open: en
  Adder #(.width(32)) adder_1 (.a(register_1_q), .b(32'h4), .out(adder_1_out));  // open: cin, cout
  Clock clock_1 (.out(clock_1_out));
  // MIPSProgramROM mipsprogramrom_1: pin names not known; wires that end beside it: register_1_q, {OPCODE, Origem2, Origem1, Reg_destino, sa, funct}
  Clock clock_2 (.out(clock_2_out));
  // RegisterFile registerfile_1: pin names not known; wires that end beside it: registerfile_1_p1, in_2, clock_2_out, habilita_escrita, End_escrita, End_leitura_REGA, End_leitura_REGB, Dado_Lido_REGA, Dado_Lido_REGB
  // Mips_ALU mips_alu_1: pin names not known; wires that end beside it: Dado_Lido_REGA, Dado_Lido_REGB, registerfile_1_p1

  // Notes on the sheet:
  //   Tipo R
  //   contents of mipsprogramrom_1 (hex, n*v repeats v):
  //   addiu $2, $0, 0x0020 addu $3, $2, $1
endmodule
