// Logisim project Caminho2.circ as structural Verilog: 1 circuit, main circuit main
module main (
  input  MEN_TO_REG,
  input  MEM_W,
  input  [3:0] ALU_OP,
  input  ALU_SURC,
  input  REG_W,
  input  MEM_R,
  input  RESET,
  input  Red_dest,
  input  in_9
);

  wire CLK, registerfile_1_p7;
  wire [4:0] multiplexer_1_out;
  wire [31:0] adder_1_out, bit_extender_1_out, mips_alu_1_p4, mips_ram_1_p7, mipsprogramrom_1_p2,
       multiplexer_2_out, register_1_q, registerfile_1_p1, registerfile_1_p8;

  Register #(.width(32)) register_1 (.D(adder_1_out), .clk(CLK), .Q(register_1_q), .clr(in_9));  // open: en
  Adder #(.width(32)) adder_1 (.a(register_1_q), .b(32'h4), .out(adder_1_out));  // open: cin, cout
  Clock clock_1 (.out(CLK));
  // MIPSProgramROM mipsprogramrom_1: pin names not known; wires that end beside it: register_1_q, mipsprogramrom_1_p2
  Multiplexer #(.width(5), .enable("false")) multiplexer_1 (
    .in0(mipsprogramrom_1_p2[20:16]), .in1(mipsprogramrom_1_p2[15:11]), .out(multiplexer_1_out),
    .sel(Red_dest));
  assign bit_extender_1_out = {{16{mipsprogramrom_1_p2[15]}}, mipsprogramrom_1_p2[15:0]};  // Bit_Extender bit_extender_1
  // RegisterFile registerfile_1: pin names not known; wires that end beside it: registerfile_1_p1, CLK, REG_W, multiplexer_1_out, mipsprogramrom_1_p2[25:21], mipsprogramrom_1_p2[20:16], registerfile_1_p7, registerfile_1_p8
  Multiplexer #(.width(32), .enable("false")) multiplexer_2 (
    .in0(registerfile_1_p8), .in1(bit_extender_1_out), .out(multiplexer_2_out), .sel(ALU_SURC));
  // Mips_ALU mips_alu_1: pin names not known; wires that end beside it: registerfile_1_p7, multiplexer_2_out, ALU_OP, mips_alu_1_p4
  // MIPS_RAM mips_ram_1: pin names not known; wires that end beside it: mips_alu_1_p4[19:0], registerfile_1_p8, MEM_W, CLK, MEM_R, RESET, mips_ram_1_p7
  Multiplexer #(.width(32), .enable("false")) multiplexer_3 (
    .in0(mips_alu_1_p4), .in1(mips_ram_1_p7), .out(registerfile_1_p1), .sel(MEN_TO_REG));

  // Notes on the sheet:
  //   R
  //   I
  //   REG_W 
  //   1
  //   1
  //   REG_DEST
  //   1
  //   0
  //   ALU_SRC
  //   0
  //   1
  //   MEM_TO_REG
  //   0
  //   0
  //   contents of mipsprogramrom_1 (hex, n*v repeats v):
  //   addiu $3,$0,0x30 addiu $4,$0,0x14D2 addu $1,$2,$3 sw $1,0($4) lw $5,0($4)
  //   Tipo I
  //   Tipo R
  //   WRITEBACK
endmodule
