// Logisim project Caminho2.circ as structural Verilog: 1 circuit, main circuit main
module main (
  input  RESET,
  input  [3:0] in_2,
  input  in_3
);

  wire ALU_SRC, CLK, I_out, MEM_R, REG_DEST, REG_W, registerfile_1_p7;
  wire [4:0] multiplexer_1_out;
  wire [5:0] OPCODE;
  wire [25:0] mipsprogramrom_1_p2;
  wire [31:0] adder_1_out, bit_extender_1_out, mips_alu_1_p4, mips_ram_1_p7, multiplexer_2_out, register_1_q,
       registerfile_1_p1, registerfile_1_p8;

  Register #(.width(32)) register_1 (.D(adder_1_out), .clk(CLK), .Q(register_1_q), .clr(in_3));  // open: en
  Adder #(.width(32)) adder_1 (.a(register_1_q), .b(32'h4), .out(adder_1_out));  // open: cin, cout
  and R (REG_DEST, ~OPCODE[0], ~OPCODE[1], ~OPCODE[2], ~OPCODE[3], ~OPCODE[4], ~OPCODE[5]);  // AND_Gate
  and I (I_out, OPCODE[0], ~OPCODE[1], ~OPCODE[2], OPCODE[3], ~OPCODE[4], ~OPCODE[5]);  // AND_Gate
  Clock clock_1 (.out(CLK));
  or or_1 (REG_W, I_out, REG_DEST);
  not not_1 (ALU_SRC, REG_DEST);
  and and_1 (MEM_R, ALU_SRC, ~I_out);  // AND_Gate
  // MIPSProgramROM mipsprogramrom_1: pin names not known; wires that end beside it: register_1_q, {OPCODE, mipsprogramrom_1_p2}, I_out
  Multiplexer #(.width(5), .enable("false")) multiplexer_1 (
    .in0(mipsprogramrom_1_p2[20:16]), .in1(mipsprogramrom_1_p2[15:11]), .out(multiplexer_1_out),
    .sel(REG_DEST));
  assign bit_extender_1_out = {{16{mipsprogramrom_1_p2[15]}}, mipsprogramrom_1_p2[15:0]};  // Bit_Extender bit_extender_1
  // RegisterFile registerfile_1: pin names not known; wires that end beside it: registerfile_1_p1, CLK, REG_W, multiplexer_1_out, mipsprogramrom_1_p2[25:21], mipsprogramrom_1_p2[20:16], registerfile_1_p7, registerfile_1_p8
  Multiplexer #(.width(32), .enable("false")) multiplexer_2 (
    .in0(registerfile_1_p8), .in1(bit_extender_1_out), .out(multiplexer_2_out), .sel(ALU_SRC));
  // Mips_ALU mips_alu_1: pin names not known; wires that end beside it: registerfile_1_p7, multiplexer_2_out, in_2, mips_alu_1_p4
  // MIPS_RAM mips_ram_1: pin names not known; wires that end beside it: mips_alu_1_p4[19:0], registerfile_1_p8, MEM_R, CLK, MEM_R, RESET, mips_ram_1_p7
  Multiplexer #(.width(32), .enable("false")) multiplexer_3 (
    .in0(mips_alu_1_p4), .in1(mips_ram_1_p7), .out(registerfile_1_p1), .sel(MEM_R));

  // Other names for the same wires on the sheet: ALU_OP[3:0] = in_2; MEM_TO_REG = MEM_R; MEM_W = MEM_R

  // Notes on the sheet:
  //   R
  //   I
  //   Load
  //   Store
  //   REG_W 
  //   1
  //   1
  //   0
  //   0
  //   REG_DEST
  //   1
  //   0
  //   0
  //   0
  //   ALU_SRC
  //   0
  //   1
  //   1
  //   1
  //   MEM_W
  //   0
  //   0
  //   0
  //   1
  //   contents of mipsprogramrom_1 (hex, n*v repeats v):
  //   addiu $2,$0,0x20  addu $3,$1,$2 addu $4,$3,$2 addu $5,$3,$4 addu $6,$4,$5 addu $7,$6,$5
  //   MEM_R
  //   0
  //   0
  //   1
  //   0
  //   MEM_TO_REG
  //   0
  //   0
  //   1
  //   0
  //   Tipo I
  //   Tipo R
  //   WRITEBACK
endmodule
